# Fritzing sketch ESP-12_to_Nokia-5110 (saved by Fritzing 0.9.2b)

parts:
  Nokia_5110_LCD_Module1 = Nokia5110LCDModule
  U1 = ESP8266-12 WiFi Module [part_number=ESP8266]

nets:
  VCC: Nokia_5110_LCD_Module1.Vcc, U1.VCC
  N1: Nokia_5110_LCD_Module1.Grnd, U1.GND
  N2: Nokia_5110_LCD_Module1.SCE, U1.GPIO_1
  N3: Nokia_5110_LCD_Module1.SCLK, U1.GPIO_5

notes:
  Nokia 5150 ESP-12
  ------------------------------------------
  PIN_SCE 5 //D1
  PIN_RESET 4 //D2
  PIN_DC 0 //D3
  PIN_SDIN 2 //D4
  PIN_SCLK 14 //D5

custom parts:
  : Nokia 5110 LCD with 8 pin. It's a 45mm*45mm module part. Description: The Nokia 5110 is a basic graphic LCD screen for lots of applications. It was originally intended for as a cell phone screen. This one is mounted on an easy to solder PCB. It uses the PCD8544 controller. The PCD8544 is a low power CMOS LCD controller/driver, designed to drive a graphic display of 48 rows and 84 columns. All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
  ESP8266-12 WiFi Module: Generic WiFi Module based on the ESP8266 with onboard PCB antenna and UART communications
